# Fritzing sketch StepperMotorSteeringCircuit (saved by Fritzing 0.9.3b)
breadboards: 1

parts:
  Part1 = Arduino Nano (Rev3.0)
  R1 = Rotary Potentiometer (Small) [maximum_resistance=100kΩ package=THT]
  M1 = Stepper Motor - Bipolar
  IC1 = H-Bridge [part_number=MA860H package=THT]

nets:
  GND: Part1.GND, R1.leg2, IC1.GND2, IC1.2A
  N1: Part1.D6, IC1.2Y
  N2: Part1.D7, IC1.VCC2
  N3: Part1.5V, R1.leg1
  N4: Part1.A5, R1.wiper
  N5: M1.A, IC1.1_2EN
  N6: M1.C, IC1.1A
  N7: M1.B, IC1.1Y
  N8: M1.D, IC1.GND1

notes:
  This microstep driver is the MA860H
  Between the wires for the motor and the wires to the arduino is ground on the left for the power supply and red on the right
